// Logisim project Relogio.circ as structural Verilog: 3 circuits, main circuit main
module Contador0_9 (
  input  Reset,
  input  Clock,
  output B,
  output A,
  output D,
  output C
);

  wire and_1_out, and_2_out, and_3_out, and_4_out, or_1_out;

  J_K_Flip_Flop j_k_ff_1 (.J(1'b1), .clk(Clock), .K(1'b1), .Q(D), .reset(or_1_out));  // open: Qn, preset, en
  and and_1 (and_1_out, C, A);
  J_K_Flip_Flop j_k_ff_2 (.J(D), .clk(Clock), .K(D), .Q(C), .reset(or_1_out));  // open: Qn, preset, en
  and and_2 (and_2_out, D, C);
  and and_3 (and_3_out, and_2_out, B);
  J_K_Flip_Flop j_k_ff_3 (.J(and_2_out), .clk(Clock), .K(and_2_out), .Q(B), .reset(or_1_out));  // open: Qn, preset, en
  J_K_Flip_Flop j_k_ff_4 (.J(and_3_out), .clk(Clock), .K(and_3_out), .Q(A), .reset(or_1_out));  // open: Qn, preset, en
  and and_4 (and_4_out, B, A);
  or or_1 (or_1_out, and_4_out, and_1_out, Reset);
endmodule

module main (
  input  in_1
);

  wire and_1_out, and_2_out, and_3_out, and_4_out, and_5_out, and_6_out, and_7_out, and_8_out, and_9_out,
       contador0_9_1_a, contador0_9_1_b, contador0_9_1_c, contador0_9_1_d, not_1_out, not_2_out, not_3_out,
       not_4_out, not_5_out, not_6_out, not_7_out, not_8_out, not_9_out, or_1_out, or_2_out, or_3_out,
       or_4_out, or_5_out, or_6_out, or_7_out, xnor_1_out, xnor_2_out, xor_1_out;

  Contador0_9 contador0_9_1 (
    .C(contador0_9_1_c), .B(contador0_9_1_b), .A(contador0_9_1_a), .Clock(in_1), .D(contador0_9_1_d));  // open: Reset
  not not_1 (not_1_out, contador0_9_1_d);
  not not_2 (not_2_out, contador0_9_1_c);
  not not_3 (not_3_out, contador0_9_1_b);
  not not_4 (not_4_out, contador0_9_1_b);
  not not_5 (not_5_out, contador0_9_1_d);
  and and_1 (and_1_out, contador0_9_1_c, not_5_out);
  not not_6 (not_6_out, contador0_9_1_b);
  and and_2 (and_2_out, contador0_9_1_c, not_5_out);
  and and_3 (and_3_out, contador0_9_1_b, not_2_out);
  and and_4 (and_4_out, not_2_out, not_5_out);
  xor xor_1 (xor_1_out, contador0_9_1_c, contador0_9_1_b);
  not not_7 (not_7_out, contador0_9_1_c);
  and and_5 (and_5_out, contador0_9_1_b, not_7_out, contador0_9_1_d);
  and and_6 (and_6_out, not_4_out, contador0_9_1_c);
  not not_8 (not_8_out, contador0_9_1_d);
  and and_7 (and_7_out, not_6_out, not_8_out);
  and and_8 (and_8_out, contador0_9_1_b, not_1_out);
  and and_9 (and_9_out, not_4_out, not_5_out);
  xnor xnor_1 (xnor_1_out, contador0_9_1_b, contador0_9_1_d);
  or or_1 (or_1_out, contador0_9_1_a, contador0_9_1_c, xnor_1_out);
  not not_9 (not_9_out, contador0_9_1_c);
  or or_2 (or_2_out, and_7_out, and_2_out);
  xnor xnor_2 (xnor_2_out, contador0_9_1_d, contador0_9_1_c);
  _7_Segment_Display u_7_segment_display_1 (
    .g(or_6_out), .f(or_5_out), .a(or_1_out), .b(or_7_out), .e(or_2_out), .d(or_4_out), .c(or_3_out));  // open: dp
  or or_3 (or_3_out, contador0_9_1_b, contador0_9_1_d, not_9_out);
  or or_4 (or_4_out, and_9_out, and_5_out, and_6_out, and_1_out, contador0_9_1_a);
  or or_5 (or_5_out, and_8_out, and_3_out, and_4_out, contador0_9_1_a);
  or or_6 (or_6_out, contador0_9_1_a, and_2_out, xor_1_out);
  or or_7 (or_7_out, xnor_2_out, not_3_out);
endmodule

module Contador0_6 (
  input  Reset,
  input  Clock
);

  wire j_k_ff_1_q, j_k_ff_2_q, j_k_ff_3_q, or_1_out, undriven, undriven_2;

  J_K_Flip_Flop j_k_ff_1 (
    .J(undriven), .clk(Clock), .K(undriven), .Q(j_k_ff_1_q), .reset(or_1_out));  // open: Qn, preset, en
  J_K_Flip_Flop j_k_ff_2 (
    .J(j_k_ff_1_q), .clk(Clock), .K(j_k_ff_1_q), .Q(j_k_ff_2_q), .reset(or_1_out));  // open: Qn, preset, en
  J_K_Flip_Flop j_k_ff_3 (
    .J(undriven_2), .clk(Clock), .K(undriven_2), .Q(j_k_ff_3_q), .reset(or_1_out));  // open: Qn, preset, en
  buf or_1 (or_1_out, Reset);  // OR_Gate
endmodule
